// Logisim project IT012_Lab01_25520720.circ as structural Verilog: 7 circuits, main circuit main
module main (
);
endmodule

module Warm_up (
  input  in_1,
  input  in_2,
  output F
);

  wire not_1_out;

  not not_1 (not_1_out, in_1);
  and and_1 (F, not_1_out, in_2);

  // Notes on the sheet:
  //   B
  //   A
endmodule

module TN1 (
  input  B,
  input  C,
  input  in_3,
  output out_4,
  output out_5,
  output out_6,
  output out_7,
  output out_8,
  output out_9,
  output out_10,
  output out_11,
  output out_12,
  output out_13
);

  wire nand_2_out;

  not not_1 (out_4, B);
  and and_1 (out_5, C, B);
  or or_1 (out_6, C, B);
  nand nand_1 (out_7, C, B);
  nor nor_1 (out_8, C, B);
  xor xor_1 (out_9, C, B);
  xnor xnor_1 (out_10, C, B);
  xor xor_2 (out_11, in_3, C, B);
  nand nand_2 (nand_2_out, B, C);
  nand nand_3 (out_13, in_3, C, B);
  nand nand_4 (out_12, nand_2_out, in_3);

  // Notes on the sheet:
  //   A
endmodule

module TN2 (
  input  X,
  input  Y,
  input  Z,
  output out_4,
  output out_5,
  output out_6,
  output out_7,
  output R4,
  output out_9
);

  wire and_1_out, and_2_out, L1_out, L2_out, L3_out, L4_5_out, not_1_out, not_2_out, or_1_out, or_2_out,
       R1_out, R2_out, R3_out, R5_out;

  not not_1 (not_1_out, X);
  not not_2 (not_2_out, Y);
  and and_1 (and_1_out, Z, Y);
  or or_1 (or_1_out, Y, X);
  or or_2 (or_2_out, Z, X);
  and and_2 (and_2_out, Y, not_1_out);
  nor L1 (L1_out, Y, X);
  and R1 (R1_out, not_2_out, not_1_out);
  nand L2 (L2_out, Y, X);
  and R2 (R2_out, not_2_out, not_1_out);
  or L3 (L3_out, and_1_out, X);
  and R3 (R3_out, or_1_out, or_2_out);
  or L4_5 (L4_5_out, and_2_out, X);
  or R5 (R5_out, Y, X);
  xnor EQ2 (out_5, L2_out, R2_out);
  xnor EQ3 (out_6, L3_out, R3_out);
  xnor EQ4 (out_7, L4_5_out, X);
  xnor EQ5 (out_9, L4_5_out, R5_out);
  xnor EQ1 (out_4, L1_out, R1_out);

  assign R4 = X;
endmodule

module TN3 (
  input  D,
  input  A,
  input  B,
  input  C,
  output F
);

  wire and_1_out, and_2_out, and_3_out, and_4_out, and_5_out, and_6_out, not_1_out, not_2_out, not_3_out,
       not_4_out;

  not not_1 (not_1_out, B);
  not not_2 (not_2_out, A);
  not not_3 (not_3_out, C);
  not not_4 (not_4_out, D);
  and and_1 (and_1_out, not_2_out, not_1_out, C, not_4_out);
  and and_2 (and_2_out, not_2_out, not_1_out, C, D);
  and and_3 (and_3_out, not_2_out, B, C, D);
  and and_4 (and_4_out, not_2_out, B, C, D);
  and and_5 (and_5_out, A, not_1_out, C, D);
  and and_6 (and_6_out, A, B, not_3_out, D);
  or or_1 (F, and_1_out, and_2_out, and_3_out, and_4_out, and_5_out, and_6_out);
endmodule

module TN4 (
  input  A,
  input  B,
  input  C,
  input  D,
  output out_5
);

  wire and_1_out, and_2_out, and_3_out, and_4_out, and_5_out, and_6_out, and_7_out, and_8_out, and_9_out,
       and_10_out, and_11_out, not_1_out, not_2_out, not_3_out, not_4_out, or_1_out, or_2_out, or_3_out,
       or_4_out, or_5_out, or_6_out, or_7_out;

  not not_1 (not_1_out, B);
  not not_2 (not_2_out, A);
  not not_3 (not_3_out, C);
  not not_4 (not_4_out, D);
  and and_1 (and_1_out, not_4_out, C, not_1_out, not_2_out);
  and and_2 (and_2_out, D, C, not_1_out, not_2_out);
  and and_3 (and_3_out, D, not_3_out, B, not_2_out);
  and and_4 (and_4_out, D, C, B, not_2_out);
  and and_5 (and_5_out, D, C, not_1_out, A);
  and and_6 (and_6_out, D, not_3_out, B, A);
  and and_7 (and_7_out, C, not_1_out, not_2_out);
  and and_8 (and_8_out, D, C, not_1_out);
  and and_9 (and_9_out, D, B, not_2_out);
  and and_10 (and_10_out, D, not_3_out, B);
  or or_1 (or_1_out, D, C);
  or or_2 (or_2_out, C, B);
  or or_3 (or_3_out, D, not_1_out);
  or or_4 (or_4_out, D, not_2_out);
  or or_5 (or_5_out, not_3_out, not_1_out, not_2_out);
  or or_6 (or_6_out, and_1_out, and_2_out, and_3_out, and_4_out, and_5_out, and_6_out);
  or or_7 (or_7_out, and_7_out, and_8_out, and_9_out, and_10_out);
  and and_11 (and_11_out, or_1_out, or_2_out, or_3_out, or_4_out, or_5_out);
  NotExactlyOne xnor_1 (.out(out_5), .in0(or_6_out), .in1(or_7_out), .in2(and_11_out));

  // Notes on the sheet:
  //   SoP_toigian
  //   F_can
endmodule

module TN5 (
  input  in_1,
  input  in_2,
  input  in_3,
  output out_4,
  output out_5
);

  wire and_1_out, and_2_out, and_3_out, and_4_out, not_1_out, not_2_out, not_3_out, xor_1_out;

  not not_1 (not_1_out, in_1);
  not not_2 (not_2_out, in_2);
  not not_3 (not_3_out, in_3);
  and and_1 (and_1_out, in_3, not_2_out, not_1_out);
  and and_2 (and_2_out, not_3_out, in_2, not_1_out);
  and and_3 (and_3_out, not_3_out, not_2_out, in_1);
  and and_4 (and_4_out, in_3, in_2, in_1);
  xor xor_1 (xor_1_out, in_3, in_2);
  or or_1 (out_4, and_1_out, and_2_out, and_3_out, and_4_out);
  xor xor_2 (out_5, xor_1_out, in_1);
endmodule
